// Logisim project CyProcessingUnit.circ as structural Verilog: 7 circuits, main circuit main
module main (
  input  in_1,
  input  in_2,
  input  in_3,
  output [7:0] A,
  output [7:0] B,
  output [7:0] C
);

  wire alu_1_error, decoder_operation_1_jump, decoder_operation_1_store, registerband_8bit_1_s_1bit;
  wire [1:0] decoder_operation_1_select_reg_in;
  wire [3:0] decoder_operation_1_s, decoders_1_rin1, decoders_1_rin2, decoders_1_rout;
  wire [7:0] decoders_1_addr8, decoders_1_operation, ip_1_addr_code, ip_1_adrr_data, ip_1_reg_in,
       ram_data_1_output_data;
  wire [23:0] fetch_1_a2, ram_instruction_1_a2;

  RAM_data ram_data_1 (
    .SELECTOR(ip_1_adrr_data), .STORE(decoder_operation_1_store), .INPUT_DATA(A),
    .OUTPUT_DATA(ram_data_1_output_data));
  RAM_Instruction ram_instruction_1 (.Memory_Choice(ip_1_addr_code), .WE(in_2), .RE(in_3), .A2(ram_instruction_1_a2));
  Clock clock_1 ();  // open: out
  Fetch fetch_1 (.A1(ram_instruction_1_a2), .A2(fetch_1_a2));
  Decoders decoders_1 (
    .A(fetch_1_a2), .zero(registerband_8bit_1_s_1bit), .Rout(decoders_1_rout), .ADDR8(decoders_1_addr8),
    .Rin2(decoders_1_rin2), .Rin1(decoders_1_rin1), .Operation(decoders_1_operation[3:0]),
    .Type_Op(decoders_1_operation[7:4]));  // open: Unused
  IP ip_1 (
    .ALU(C), .RAM(ram_data_1_output_data), .ADDR8(decoders_1_addr8),
    .LOAD(decoder_operation_1_select_reg_in), .Kill(in_1), .Jump(decoder_operation_1_jump),
    .REG_IN(ip_1_reg_in), .ADRR_DATA(ip_1_adrr_data), .ADDR_CODE(ip_1_addr_code));
  Decoder_Operation decoder_operation_1 (
    .A(decoders_1_operation), .S(decoder_operation_1_s), .SELECT_REG_IN(decoder_operation_1_select_reg_in),
    .STORE(decoder_operation_1_store), .JUMP(decoder_operation_1_jump));
  RegisterBand_8bit registerband_8bit_1 (
    .Data(ip_1_reg_in), .SlctA(decoders_1_rin1[2:0]), .SlctB(decoders_1_rin2[2:0]), .SlctC(decoders_1_rout),
    .A(A), .B(B), .S_1bit(registerband_8bit_1_s_1bit));
  LED led_1 (.in(alu_1_error));
  ALU alu_1 (.A(A), .B(B), .SlctOP(decoder_operation_1_s), .Error(alu_1_error), .C(C));
endmodule

module Decoder_Operation (
  input  [7:0] A,
  output [3:0] S,
  output [1:0] SELECT_REG_IN,
  output STORE,
  output JUMP
);

  wire not_1_out, not_2_out, not_3_out, not_4_out, not_5_out, not_6_out, not_7_out, not_8_out, or_1_out,
       or_2_out, or_3_out, or_4_out, or_5_out, or_6_out, or_7_out, or_8_out, or_9_out, or_10_out, or_11_out,
       or_12_out, or_13_out, or_14_out, or_15_out, or_16_out, or_17_out, or_18_out, or_19_out, or_20_out;

  not not_1 (not_1_out, A[7]);
  not not_2 (not_2_out, A[6]);
  not not_3 (not_3_out, A[5]);
  not not_4 (not_4_out, A[4]);
  not not_5 (not_5_out, A[3]);
  not not_6 (not_6_out, A[2]);
  not not_7 (not_7_out, A[1]);
  not not_8 (not_8_out, A[0]);
  or or_1 (or_1_out, A[4], A[3]);
  or or_2 (or_2_out, not_4_out, not_5_out);
  or or_3 (or_3_out, A[7], A[6], A[5], A[3], A[2], A[1], A[0]);
  or or_4 (or_4_out, A[4], not_7_out);
  or or_5 (or_5_out, not_4_out, A[1]);
  or or_6 (or_6_out, A[7], A[6], A[5], A[2], A[1], A[0]);
  or or_7 (or_7_out, A[4], A[2]);
  or or_8 (or_8_out, A[2], A[0]);
  or or_9 (or_9_out, A[2], A[0]);
  or or_10 (or_10_out, not_6_out, not_8_out);
  or or_11 (or_11_out, A[4], A[2], A[0]);
  or or_12 (or_12_out, not_6_out, not_7_out, not_8_out);
  or or_13 (or_13_out, not_5_out, not_7_out);
  or or_14 (or_14_out, not_5_out, not_6_out);
  or or_15 (or_15_out, not_4_out, not_7_out, not_8_out);
  or or_16 (or_16_out, not_4_out, not_6_out);
  or or_17 (or_17_out, not_3_out, not_8_out);
  or or_18 (or_18_out, not_3_out, not_7_out);
  or or_19 (or_19_out, A[5], not_6_out, A[1], A[0]);
  or or_20 (or_20_out, not_3_out, not_4_out);
  and and_1 (STORE, A[5], A[1], not_8_out, not_6_out, not_5_out, not_4_out, not_2_out, not_1_out);
  and and_2 (JUMP, A[5], A[2], A[0], not_7_out, not_5_out, not_4_out, not_2_out, not_1_out);
  and and_3 (S[3], or_1_out, or_2_out);
  and and_4 (S[2], or_3_out, not_4_out);
  and and_5 (S[1], or_4_out, not_5_out, or_5_out, or_6_out);
  and and_6 (S[0], or_7_out, or_8_out);
  and and_7 (SELECT_REG_IN[1], A[5], or_9_out, not_7_out, or_10_out, not_5_out, not_4_out, not_2_out, not_1_out);
  and and_8 (SELECT_REG_IN[0], or_11_out, or_12_out, or_13_out, or_14_out, or_15_out, or_16_out, or_17_out, or_18_out, not_2_out, not_1_out, or_19_out, or_20_out);
endmodule

module Fetch (
  input  [23:0] A1,
  output [23:0] A2
);

  Register_24bit register_24bit_1 (.in_1(A1), .WE(1'b1), .out_3(A2));
endmodule

module RAM_Instruction (
  input  [7:0] Memory_Choice,
  input  WE,
  input  RE,
  output [23:0] A2
);

  wire clock_1_out;

  RAM #(.dataWidth(24)) ram_1 (.addr(Memory_Choice), .we(WE), .oe(RE), .clk(clock_1_out), .dout(A2));  // open: din
  Clock clock_1 (.out(clock_1_out));
endmodule

module RAM_data (
  input  [7:0] SELECTOR,
  input  STORE,
  input  [7:0] INPUT_DATA,
  output [7:0] OUTPUT_DATA
);

  wire clock_1_out;

  RAM ram_1 (.addr(SELECTOR), .we(STORE), .clk(clock_1_out), .din(INPUT_DATA), .dout(OUTPUT_DATA));  // open: oe
  Clock clock_1 (.out(clock_1_out));
endmodule

module Decoders (
  input  [23:0] A,
  input  zero,
  output [3:0] Rout,
  output [7:0] ADDR8,
  output [3:0] Unused,
  output [3:0] Rin2,
  output [3:0] Rin1,
  output [3:0] Operation,
  output [3:0] Type_Op
);

  Register_24bit register_24bit_1 (.in_1(A), .WE(1'b1), .out_3({Type_Op, Operation, Rin1, ADDR8, Rout}));
  Clock clock_1 ();  // open: out

  assign Rin2 = ADDR8[7:4];
  assign Unused = ADDR8[3:0];
endmodule

module IP (
  input  [7:0] ALU,
  input  [7:0] RAM,
  input  [7:0] ADDR8,
  input  [1:0] LOAD,
  input  Kill,
  input  Jump,
  output [7:0] REG_IN,
  output [7:0] ADRR_DATA,
  output [7:0] ADDR_CODE
);

  wire clock_1_out;
  wire [7:0] counter_1_q, register_8bit_1_out_3;

  Multiplexer #(.width(8)) multiplexer_1 (.in0(counter_1_q), .in1(ADDR8), .out(ADDR_CODE), .sel(Jump));
  Register_8bit register_8bit_1 (.in_1(ADDR_CODE), .WE(1'b1), .out_3(register_8bit_1_out_3));
  Clock clock_1 (.out(clock_1_out));
  Multiplexer #(.select(2)) multiplexer_2 ();  // open: in0, in1, in2, in3, out, sel
  Counter counter_1 (
    .D(register_8bit_1_out_3), .Q(counter_1_q), .clk(clock_1_out), .clr(Kill));  // open: load, count, carry, up
  Multiplexer #(.select(2), .width(8)) multiplexer_3 (
    .in1(ALU), .in2(RAM), .in3(ADDR8), .out(REG_IN), .sel(LOAD));  // open: in0

  assign ADRR_DATA = ADDR8;
endmodule
