// Logisim project OperatorLib.circ as structural Verilog: 1 circuit, main circuit AND_Operator
module AND_Operator (
  input  [7:0] A,
  input  [7:0] B
);

  wire [0:0] and_1_out;

  and and_1 (and_1_out[0], A[0], B[0]);
endmodule
