// Logisim project RegisterLib.circ as structural Verilog: 2 circuits, main circuit Register_8bit
module Register_8bit (
  input  [7:0] in_1,
  input  WE,
  output [7:0] out_3
);

  wire and_1_out, clock_1_out;

  Clock clock_1 (.out(clock_1_out));
  and and_1 (and_1_out, clock_1_out, WE);
  D_Flip_Flop d_ff_1 (.D(in_1[0]), .clk(and_1_out), .Q(out_3[0]));  // open: Qn, preset, reset
  D_Flip_Flop d_ff_2 (.D(in_1[1]), .clk(and_1_out), .Q(out_3[1]));  // open: Qn, preset, reset
  D_Flip_Flop d_ff_3 (.D(in_1[2]), .clk(and_1_out), .Q(out_3[2]));  // open: Qn, preset, reset
  D_Flip_Flop d_ff_4 (.D(in_1[3]), .clk(and_1_out), .Q(out_3[3]));  // open: Qn, preset, reset
  D_Flip_Flop d_ff_5 (.D(in_1[4]), .clk(and_1_out), .Q(out_3[4]));  // open: Qn, preset, reset
  D_Flip_Flop d_ff_6 (.D(in_1[5]), .clk(and_1_out), .Q(out_3[5]));  // open: Qn, preset, reset
  D_Flip_Flop d_ff_7 (.D(in_1[6]), .clk(and_1_out), .Q(out_3[6]));  // open: Qn, preset, reset
  D_Flip_Flop d_ff_8 (.D(in_1[7]), .clk(and_1_out), .Q(out_3[7]));  // open: Qn, preset, reset
endmodule

module RegisterBand_bit (
  input  [7:0] Data,
  input  [1:0] SlctC,
  input  [1:0] SlctA,
  input  [1:0] SlctB,
  output [7:0] A,
  output [7:0] B
);

  wire decoder_1_out0, decoder_1_out1, decoder_1_out2, decoder_1_out3;
  wire [7:0] register_8bit_1_out_3, register_8bit_2_out_3, register_8bit_3_out_3, register_8bit_4_out_3;

  Decoder #(.select(2)) decoder_1 (
    .out0(decoder_1_out0), .out1(decoder_1_out1), .out2(decoder_1_out2), .out3(decoder_1_out3), .sel(SlctC));  // open: en
  Register_8bit register_8bit_1 (.in_1(Data), .WE(decoder_1_out0), .out_3(register_8bit_1_out_3));
  Register_8bit register_8bit_2 (.in_1(Data), .WE(decoder_1_out1), .out_3(register_8bit_2_out_3));
  Register_8bit register_8bit_3 (.in_1(Data), .WE(decoder_1_out2), .out_3(register_8bit_3_out_3));
  Register_8bit register_8bit_4 (.in_1(Data), .WE(decoder_1_out3), .out_3(register_8bit_4_out_3));
  Multiplexer #(.select(2), .width(8)) multiplexer_1 (
    .in0(register_8bit_1_out_3), .in1(register_8bit_2_out_3), .in2(register_8bit_3_out_3),
    .in3(register_8bit_4_out_3), .out(A), .sel(SlctA));
  Multiplexer #(.select(2), .width(8)) multiplexer_2 (
    .in0(register_8bit_1_out_3), .in1(register_8bit_2_out_3), .in2(register_8bit_3_out_3),
    .in3(register_8bit_4_out_3), .out(B), .sel(SlctB));
endmodule
