// Logisim project SubtractorLib.circ as structural Verilog
module substractor_8bit (
  input  [7:0] A,
  input  [7:0] B,
  output Error,
  output [7:0] S
);

  wire add_8bits_1_overflow, and_2_out, complement_2_1_overflow, not_2_out;
  wire [7:0] and_1_out, complement_2_1_a_to_2;

  assign and_1_out = {8{1'b0}} & B;  // AND_Gate and_1, 8 bits wide
  // NOT_Gate not_1 has open pins: in=and_1_out, out=open
  complement_2 complement_2_1 (.A(B), .A_to_2(complement_2_1_a_to_2), .Overflow(complement_2_1_overflow));
  buf and_2 (and_2_out, complement_2_1_overflow);  // AND_Gate
  or or_1 (Error, and_2_out, not_2_out);
  not not_2 (not_2_out, add_8bits_1_overflow);
  Add_8bits add_8bits_1 (.A(complement_2_1_a_to_2), .B(A), .S(S), .Overflow(add_8bits_1_overflow));
endmodule

module complement_2 (
  input  [7:0] A,
  output [7:0] A_to_2,
  output Overflow
);

  wire [7:0] not_1_out;

  assign not_1_out = ~A;  // NOT_Gate not_1, 8 bits wide
  Add_8bits add_8bits_1 (.A(not_1_out), .B(8'h1), .S(A_to_2), .Overflow(Overflow));
endmodule
